# Fritzing sketch 4-digit-7-segment-schematic (saved by Fritzing 0.9.2b)
breadboards: 1

parts:
  LED = mystery part, 12 pins [chip_label=LED part_number=D5641CSR]
  Part1 = Arduino Uno (Rev3)
  R1 = Resistor [tolerance=±5% resistance=330 package=THT]
  R2 = Resistor [tolerance=±5% resistance=330 package=THT]
  R3 = Resistor [tolerance=±5% resistance=330 package=THT]
  R4 = Resistor [tolerance=±5% resistance=330 package=THT]
  R5 = Resistor [tolerance=±5% resistance=330 package=THT]
  R6 = Resistor [tolerance=±5% resistance=330 package=THT]
  R7 = Resistor [tolerance=±5% resistance=330 package=THT]
  R8 = Resistor [tolerance=±5% resistance=330 package=THT]

nets:
  N1: LED.pin1, R5.Pin_1
  N2: LED.pin2, R4.Pin_1
  N3: LED.pin3, R8.Pin_1
  N4: LED.pin4, R3.Pin_1
  N5: LED.pin5, R7.Pin_1
  N6: LED.pin6, Part1.D13/SCK
  N7: LED.pin7, R2.Pin_1
  N8: LED.pin8, Part1.D12/MISO
  N9: LED.pin9, Part1.D11_PWM/MOSI
  N10: LED.pin10, R6.Pin_1
  N11: LED.pin11, R1.Pin_1
  N12: LED.pin12, Part1.D10_PWM/SS
  N13: Part1.D8, R7.Pin_0
  N14: Part1.D9_PWM, R8.Pin_0
  N15: Part1.D2, R1.Pin_0
  N16: Part1.D3_PWM, R2.Pin_0
  N17: Part1.D4, R3.Pin_0
  N18: Part1.D5_PWM, R4.Pin_0
  N19: Part1.D6_PWM, R5.Pin_0
  N20: Part1.D7, R6.Pin_0
